# Fritzing sketch MarioTouch (saved by Fritzing 0.7.10b)
breadboards: 1

parts:
  Arduino1 = Arduino
  J1 = Piezo Speaker
  U1 = DS_TOUCH_CONNECTOR [package=ds_touch_connector]
  R1 = Resistor [tolerance=±5% resistance=10k package=THT]
  R2 = Resistor [tolerance=±5% resistance=10k package=THT]
  R3 = Resistor [tolerance=±5% resistance=10k package=THT]
  R4 = Resistor [tolerance=±5% resistance=10k package=THT]

nets:
  N1: Arduino1.GND, J1.pin1, R1.Pin_0, R2.Pin_0, R3.Pin_0, R4.Pin_0
  N2: Arduino1.D9, J1.pin2
  N3: Arduino1.A0, U1.X1, R1.Pin_1
  N4: Arduino1.A1, U1.X2, R2.Pin_1
  N5: Arduino1.A2, U1.Y1, R3.Pin_1
  N6: Arduino1.A3, U1.Y2, R4.Pin_1
